# Fritzing sketch Drone_JoyStick (saved by Fritzing 1.0.2b)

parts:
  Part1 = Thumb Joystick
  Part2 = Thumb Joystick
  Part3 = Arduino Nano (Rev3.0)
  VCC1 = Battery
  S1 = Pushbutton [package="[THT]"]
  S2 = Pushbutton [package="[THT]"]
  S3 = Pushbutton [package="[THT]"]
  S4 = Toggle Switch [package=THT]

nets:
  GND: Part1.GND, Part2.GND, Part3.GND, VCC1.-, S1.Pin_2, S2.Pin_2, S3.Pin_2
  N1: Part1.SEL, Part3.D2
  N2: Part1.HORZ, Part3.A0
  N3: Part1.VERT, Part3.A1
  VCC: Part1.VCC, Part2.VCC, Part3.5V
  N4: Part2.SEL, Part3.D3
  N5: Part2.HORZ, Part3.A2
  N6: Part2.VERT, Part3.A3
  N7: Part3.VIN, S4.L2
  N8: Part3.A4, S1.Pin_4, S2.Pin_4, S3.Pin_4
  N9: VCC1.+, S4.COM

notes:
  Джойстик кутовий
  Джойстик потужності
